# Fritzing sketch câblage (saved by Fritzing 0.9.8b)
breadboards: 1

parts:
  Composant1 = Arduino BT
  DFRobot_DFPlayer_Mini1 = DFRobot DFPlayer Mini [part_number=DFR0299]

nets:
  N1: Composant1.SS/PWM_D10, DFRobot_DFPlayer_Mini1.TX
  N2: Composant1.MOSI/PWM_D11, DFRobot_DFPlayer_Mini1.VCC, DFRobot_DFPlayer_Mini1.RX
